# Fritzing sketch Single_Tube_Diagram (saved by Fritzing 0.9.3b)
breadboards: 1

parts:
  IC1 = IC, DIP package, 16 pins [chip_label=K155ID1]
  Part1 = Arduino Uno (Rev3)
  LED1 = smd LED [color="Blue (430nm)" package="0805 [SMD]"]
  R1 = Resistor [tolerance=±5% resistance=10k package=THT]
  D1 = Rectifier Diode [part_number=1N4001 package="300 mil [THT]"]
  LED2 = smd LED [color="Blue (430nm)" package="0805 [SMD]"]
  R2 = Resistor [tolerance=±5% resistance=10k package=THT]
  J2 = screw terminal, 12 pins
  R3 = Resistor [tolerance=±5% resistance=10k package=THT]
  KEYPAD1 = Membrane Matrix Keypad
  IC2 = IC, DIP package, 4 pins [chip_label=DC]

nets:
  N1: IC1.pin1, J2.pin9
  N2: IC1.pin2, J2.pin10
  N3: IC1.pin5, D1.cathode
  N4: IC1.pin8, J2.pin3
  N5: IC1.pin9, J2.pin4
  N6: IC1.pin10, J2.pin8
  N7: IC1.pin11, J2.pin7
  N8: IC1.pin12, IC2.pin3
  N9: IC1.pin13, J2.pin5
  N10: IC1.pin14, J2.pin6
  N11: IC1.pin15, J2.pin2
  N12: IC1.pin16, J2.pin1
  N13: Part1.A0, KEYPAD1.5
  N14: Part1.A1, KEYPAD1.6
  N15: Part1.A2, KEYPAD1.7
  N16: Part1.D9_PWM, R2.Pin_1
  N17: Part1.D10_PWM/SS, R1.Pin_1
  N18: Part1.D4, KEYPAD1.4
  N19: Part1.D5_PWM, KEYPAD1.3
  N20: Part1.D6_PWM, KEYPAD1.2
  N21: Part1.D7, KEYPAD1.1
  N22: Part1.5V, LED1.anode, D1.anode, LED2.anode, IC2.pin1
  N23: Part1.GND, IC2.pin2
  N24: LED1.cathode, R1.Pin_0
  N25: LED2.cathode, R2.Pin_0
  N26: J2.pin12, R3.Pin_1
  N27: R3.Pin_0, IC2.pin4

notes:
  0. 1. 2. 3. 4. 5. 6. 7. 8. 9. D. A
  Nixie Tube Connector

custom parts:
  Membrane Matrix Keypad: Membrane Matrix 3x4 Keypad
